# Fritzing sketch schematic (saved by Fritzing 0.9.3b)
breadboards: 1

parts:
  U1 = NodeMCU V1.0
  PCB2 = RTC_DS1302_module
  GY1 = GY-521 (MPU-6050) [form="♀ (female)" package=THT]
  Part1 = MicroSD Card Module

nets:
  N1: U1.D1, GY1.pin3
  N2: U1.D2, GY1.pin4
  N3: U1.D3, PCB2.DAT
  N4: U1.D4, PCB2.CLK
  VCC: U1.3V3, PCB2.VCC, GY1.pin1, Part1.VCC
  GND: U1.GND, PCB2.GND, GY1.pin2, Part1.GND
  N5: U1.D5, Part1.SCK
  N6: U1.D6, Part1.MISO
  N7: U1.D7, Part1.MOSI
  N8: U1.D8, Part1.CS
  N9: U1.RX, PCB2.RST

custom parts:
  NodeMCU V1.0: ESP8266 based NodeMCU
  RTC_DS1302_module: Arduino module DS1302 SPI Real Time Clock
  GY-521 (MPU-6050): Placa GY-521 basada en conjunto de acelerómetro+giroscopios MPU-6050
  MicroSD Card Module: A common microSD card module.
